# Fritzing sketch MacroCloud (saved by Fritzing 1.0.6)

parts:
  RE3 = Rotary Encoder dual with switch [package=THT]
  S9 = Pushbutton [package="[SMD]"]
  S10 = Pushbutton [package="[SMD]"]
  S11 = Pushbutton [package="[SMD]"]
  S12 = 0.91 inch OLED I2C Display 128 x 32 Pixels
  SG3 = Buzzer 12mm [part_number=COM-07950 package=buzzer-12mm-ns]
  U3 = LIPO-110mAh [package=lipo-110]
  LED4 = LED - 5mm [color="Red (633nm)" current=0.030A package="5 mm [THT]"]
  LED5 = LED - 5mm [color="Red (633nm)" current=0.030A package="5 mm [THT]"]  # not connected
  LED6 = LED - 5mm [color="Red (633nm)" current=0.030A package="5 mm [THT]"]  # not connected
  A6 = XIAO ESP32C3-smd
  RE4 = Rotary Encoder dual with switch [package=THT]
  S13 = Pushbutton [package="[SMD]"]
  S14 = Pushbutton [package="[SMD]"]
  S15 = Pushbutton [package="[SMD]"]
  S16 = 0.91 inch OLED I2C Display 128 x 32 Pixels
  SG4 = Buzzer 12mm [part_number=COM-07950 package=buzzer-12mm-ns]
  LED7 = LED - 5mm [color="Red (633nm)" current=0.030A package="5 mm [THT]"]  # not connected
  LED8 = LED - 5mm [color="Red (633nm)" current=0.030A package="5 mm [THT]"]
  LED9 = LED - 5mm [color="Red (633nm)" current=0.030A package="5 mm [THT]"]  # not connected
  A2 = Waveshare rp2040-zero tht [package=THT]

nets:
  N1: RE3.Encoder1PinA, A6.Pin_15
  N2: RE3.Encoder1PinB, RE3.Encoder2PinC, S9.Pin_1, S9.Pin_2, S10.Pin_1, S10.Pin_2, S11.Pin_1, S11.Pin_2, SG3.2
  N3: RE3.Encoder2PinA, A6.Pin_11
  N4: RE3.Encoder2PinB, A6.Pin_10
  N5: S9.Pin_3, S9.Pin_4, A6.Pin_13
  N6: S10.Pin_3, S10.Pin_4, A6.Pin_12
  N7: S11.Pin_3, S11.Pin_4, A6.Pin_14
  N8: S12.VCC, LED4.anode
  N9: S12.GND, A6.Pin_21
  N10: S12.SDA, A6.Pin_18
  N11: S12.SCL, A6.Pin_19
  N12: SG3.1, A6.Pin_16
  N13: U3.+, A6.Pin_8
  N14: U3.-, A6.Pin_7
  N15: LED4.cathode, A6.Pin_17
  N16: RE4.Encoder1PinB, RE4.Encoder2PinC, S13.Pin_1, S13.Pin_2, S14.Pin_1, S14.Pin_2, S15.Pin_1, S15.Pin_2, SG4.2
  N17: RE4.Encoder2PinA, A2.Pin_19
  N18: RE4.Encoder2PinB, A2.Pin_18
  N19: S13.Pin_3, S13.Pin_4, A2.Pin_21
  N20: S14.Pin_3, S14.Pin_4, A2.Pin_20
  N21: S15.Pin_3, S15.Pin_4, A2.Pin_22
  N22: S16.VCC, LED8.anode
  N23: S16.GND, A2.Pin_2
  N24: S16.SDA, A2.Pin_8
  N25: S16.SCL, A2.Pin_7
  N26: SG4.1, A2.Pin_5
  N27: LED8.cathode, A2.Pin_6

custom parts:
  Rotary Encoder dual with switch: Dual rotary Encoder ALPS-EC11EBB24C03 with switch.
  Buzzer 12mm: Buzzer 12mm Spark Fun Electronics SKU : Comp-Buzzer Through hole This is a small 12mm round speaker that operates around the audible 2kHz range. You can use these speakers to create simple music or user interfaces. This is not a true piezoelectric speaker but behaves similarly. Instead of a piezoelectric crystal that vibrates with an electric current, this tiny speaker uses an electromagnet to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
  XIAO ESP32C3-smd: Seeed Studio XIAO ESP32C3 adopts new RISC-V architecture, supporting both Wi-Fi and BLE wireless connectivities.
  Waveshare rp2040-zero tht: .RP2040-Zero, A Low-Cost, High-Performance Pico-Like MCU Board Based On Raspberry Pi Microcontroller RP2040. This varant is THT without the extra connections.
